# Fritzing sketch schematics (saved by Fritzing 0.9.2b)
breadboards: 1

parts:
  Part1 = Arduino Nano (Rev3.0)
  Mod1 = KY-019 5V Relay Module [package="Breakout board"]
  U2 = LIPO-1000mAh [package=lipo-1000]
  M1 = sim800L v2 evb
  S1 = Reed switch [package=THT]
  S2 = Pushbutton [package="[THT]"]
  U3 = Mini-360 DC-DC Buck converter [package=THT]
  J1 = Piezo Speaker

nets:
  N1: Part1.GND, Mod1.-, M1.pin_2, M1.pin_6, S1.pin_2, S2.Pin_1, S2.Pin_2, U3.OUT-
  N2: Part1.D2, S1.pin_1
  N3: Part1.D3, S2.Pin_3, S2.Pin_4
  N4: Part1.D4, Mod1.S
  N5: Part1.D11/MOSI, M1.pin_4
  N6: Part1.D12/MISO, M1.pin_3
  N7: Part1.VIN, M1.pin_7, U3.OUT+
  N8: Part1.5V, Mod1.+
  N9: Mod1.Common, U2.+, U3.IN+
  N10: Mod1.NO, J1.pin2
  N11: U2.-, U3.IN-, J1.pin1

notes:
  12V battery
  Siren
  Reed Switch
  IN -> 5V

custom parts:
  KY-019 5V Relay Module: KY-019 5V Relay module, used to control AC circuits. (Special thanks to vanepp for fixing the PCB holes and other errors)
  sim800L v2 evb: sim800L v2 evb GSM module.
  Mini-360 DC-DC Buck converter: Mini-360 DC-DC Buck converter. Tiny buck step down voltage converter, input voltage 4.75 to 23V output 1 to 17V adjustable. Available from ebay and the like.
